// Logisim project project2.circ as structural Verilog: 1 circuit, main circuit main
module main (
  output [7:0] out_1,
  output [7:0] out_2,
  output Reg2Loc,
  output RegWrite,
  output ALUop,
  output [7:0] RegData1,
  output [1:0] WriteReg,
  output [7:0] RegDataW,
  output [7:0] ReadDataM,
  output [7:0] ALUout,
  output ALUSrc,
  output [7:0] RegData2,
  output MemRead,
  output MemWrite,
  output MemToReg,
  output [7:0] imm8,
  output [1:0] Rn,
  output [1:0] Rm,
  output [1:0] ReadReg2,
  output [1:0] Rd,
  output [1:0] ReadReg1
);

  wire and_1_out, and_2_out, and_3_out, and_4_out, clock_1_out, decoder_1_out0, decoder_1_out1,
       decoder_1_out2, decoder_1_out3, not_1_out, not_2_out, not_3_out, not_4_out, not_5_out;
  wire [2:0] ram_1_dout;
  wire [7:0] adder_2_out, multiplexer_4_out, register_1_q, subtractor_1_out, X0_q, X1_q, X2_q, X3_q;

  Register register_1 (.D(out_2), .en(1'b1), .clk(clock_1_out), .Q(register_1_q));  // open: clr
  Adder adder_1 (.a(8'h1), .b(register_1_q), .out(out_2));  // open: cin, cout
  RAM #(.dataWidth(24), .enables("line")) ram_1 (
    .addr(register_1_q), .we(1'b0), .clk(clock_1_out),
    .dout({Reg2Loc, ALUop, RegWrite, ALUSrc, MemRead, MemWrite, MemToReg, imm8, ReadReg1, Rm, Rd, ram_1_dout}));  // open: din
  Multiplexer #(.width(2)) multiplexer_1 (.in0(Rd), .in1(Rm), .out(ReadReg2), .sel(Reg2Loc));
  Decoder #(.select(2)) decoder_1 (
    .out0(decoder_1_out0), .out1(decoder_1_out1), .out2(decoder_1_out2), .out3(decoder_1_out3), .sel(Rd));  // open: en
  Clock clock_1 (.out(clock_1_out));
  and and_1 (and_1_out, RegWrite, decoder_1_out0);
  and and_2 (and_2_out, RegWrite, decoder_1_out1);
  and and_3 (and_3_out, RegWrite, decoder_1_out2);
  and and_4 (and_4_out, RegWrite, decoder_1_out3);
  Register X0 (.D(RegDataW), .en(and_1_out), .clk(clock_1_out), .Q(X0_q));  // open: clr
  Register X1 (.D(RegDataW), .en(and_2_out), .clk(clock_1_out), .Q(X1_q));  // open: clr
  Register X2 (.D(RegDataW), .en(and_3_out), .clk(clock_1_out), .Q(X2_q));  // open: clr
  Register X3 (.D(RegDataW), .en(and_4_out), .clk(clock_1_out), .Q(X3_q));  // open: clr
  Multiplexer #(.select(2), .width(8)) multiplexer_2 (
    .in0(X0_q), .in1(X1_q), .in2(X2_q), .in3(X3_q), .out(RegData1), .sel(ReadReg1));
  Multiplexer #(.select(2), .width(8)) multiplexer_3 (
    .in0(X0_q), .in1(X1_q), .in2(X2_q), .in3(X3_q), .out(RegData2), .sel(ReadReg2));
  Multiplexer #(.width(8)) multiplexer_4 (.in0(RegData2), .in1(imm8), .out(multiplexer_4_out), .sel(ALUSrc));
  Adder adder_2 (.a(RegData1), .b(multiplexer_4_out), .out(adder_2_out));  // open: cin, cout
  Subtractor subtractor_1 (.a(RegData1), .b(multiplexer_4_out), .out(subtractor_1_out));  // open: bin, bout
  Multiplexer #(.width(8)) multiplexer_5 (.in0(adder_2_out), .in1(subtractor_1_out), .out(ALUout), .sel(ALUop));
  LED led_1 (.in(clock_1_out));
  LED led_2 (.in(clock_1_out));
  LED led_3 (.in(clock_1_out));
  LED led_4 (.in(clock_1_out));
  LED led_5 (.in(clock_1_out));
  LED led_6 (.in(clock_1_out));
  RAM #(.enables("line")) Memory (.addr(ALUout), .we(MemWrite), .clk(not_1_out), .din(RegData2), .dout(ReadDataM));
  not not_1 (not_1_out, clock_1_out);
  LED led_7 (.in(not_2_out));
  LED led_8 (.in(not_2_out));
  LED led_9 (.in(not_2_out));
  LED led_10 (.in(not_2_out));
  LED led_11 (.in(not_2_out));
  LED led_12 (.in(clock_1_out));
  LED led_13 (.in(clock_1_out));
  LED led_14 (.in(clock_1_out));
  not not_2 (not_2_out, clock_1_out);
  LED led_15 (.in(not_3_out));
  LED led_16 (.in(not_3_out));
  LED led_17 (.in(not_3_out));
  LED led_18 (.in(not_3_out));
  LED led_19 (.in(not_3_out));
  LED led_20 (.in(not_2_out));
  not not_3 (not_3_out, not_2_out);
  LED led_21 (.in(not_3_out));
  LED led_22 (.in(not_3_out));
  LED led_23 (.in(not_3_out));
  LED led_24 (.in(not_3_out));
  LED led_25 (.in(not_3_out));
  LED led_26 (.in(not_3_out));
  LED led_27 (.in(not_3_out));
  LED led_28 (.in(not_3_out));
  LED led_29 (.in(not_4_out));
  LED led_30 (.in(not_4_out));
  LED led_31 (.in(not_4_out));
  LED led_32 (.in(not_4_out));
  LED led_33 (.in(not_4_out));
  LED led_34 (.in(not_4_out));
  LED led_35 (.in(not_4_out));
  LED led_36 (.in(not_4_out));
  LED led_37 (.in(not_4_out));
  LED led_38 (.in(not_4_out));
  not not_4 (not_4_out, not_3_out);
  LED led_39 (.in(not_4_out));
  LED led_40 (.in(not_4_out));
  LED led_41 (.in(not_4_out));
  LED led_42 (.in(not_4_out));
  LED led_43 (.in(not_4_out));
  LED led_44 (.in(not_4_out));
  LED led_45 (.in(not_4_out));
  LED led_46 (.in(not_4_out));
  LED led_47 (.in(not_4_out));
  LED led_48 (.in(not_5_out));
  not not_5 (not_5_out, not_4_out);
  Multiplexer #(.width(8)) multiplexer_6 (.in0(ALUout), .in1(ReadDataM), .out(RegDataW), .sel(MemToReg));
  LED led_49 (.in(not_5_out));
  LED led_50 (.in(not_5_out));
  LED led_51 (.in(not_5_out));
  LED led_52 (.in(not_5_out));
  LED led_53 (.in(not_5_out));
  LED led_54 (.in(not_5_out));
  LED led_55 (.in(not_5_out));
  LED led_56 (.in(not_5_out));
  LED led_57 (.in(not_5_out));
  LED led_58 (.in(not_5_out));
  Register register_2 (.D(RegDataW), .en(1'b1), .clk(not_5_out), .Q(out_1));  // open: clr
  LED led_59 (.in(not_5_out));
  LED led_60 (.in(not_5_out));
  _7_Segment_Display u_7_segment_display_1 ();  // open: g, f, a, b, e, d, c, dp
  _7_Segment_Display u_7_segment_display_2 ();  // open: g, f, a, b, e, d, c, dp
  // BCD_to_7_Segment_decoder bcd_to_7_segment_decoder_1: pin names not known
  // BCD_to_7_Segment_decoder bcd_to_7_segment_decoder_2: pin names not known
  // Binary_to_BCD_converter #(.binvalue(8)) binary_to_bcd_converter_1: pin names not known; wires that end beside it: out_1
  _7_Segment_Display u_7_segment_display_3 ();  // open: g, f, a, b, e, d, c, dp
  // BCD_to_7_Segment_decoder bcd_to_7_segment_decoder_3: pin names not known
  Hex_Digit_Display hex_digit_display_1 (.value(out_1[7:4]));  // open: dp
  Hex_Digit_Display hex_digit_display_2 (.value(out_1[3:0]));  // open: dp

  assign Rn = ReadReg1;
  assign WriteReg = Rd;

  // Notes on the sheet:
  //   Date: 12/02/2023
  //   CPU Title: 382 Santa 9 6900X
  //   Name: Joshua Hizgiaev & Matthew Soltys
  //   Pledge: I pledge my honor that I have abided by the Stevens Honor System.
endmodule
